# Fritzing sketch scematic (saved by Fritzing 1.0.1rc)

parts:
  Keypad4x4 = Keypad Membran 4x4
  Part1 = Arduino Uno (Rev3) - ICSP
  LCM1602_IIC1 = LCM1602 IIC [part_number="LCM1602 IIC" chip_label="LCM1602 IIC" package="DIP (Dual Inline) [THT]"]
  LED1 = LED - 5mm [color="Red (633nm)" current=0.030A package="5 mm [THT]"]
  LED2 = LED - 5mm [color="Green (555nm)" current=0.030A package="5 mm [THT]"]
  R1 = Resistor [tolerance=±5% power=0.25W resistance=220 package=THT]
  J1 = Piezo Speaker
  U1 = LCD-16X2 [package=lcd-16x2]
  M1 = xy-mos d4184 [package=THT]
  Power_plug1 = Power plug  # not connected
  L1 = Solenoid

nets (from the schematic view):
  N1: Keypad4x4.Pin1, Part1.ICSP_MOSI, Part1.D11_PWM/MOSI
  N2: Keypad4x4.Pin2, Part1.D10_PWM/SS
  N3: Keypad4x4.Pin3, Part1.D9_PWM
  N4: Keypad4x4.Pin4, Part1.D8
  N5: Keypad4x4.Pin5, Part1.D7
  N6: Keypad4x4.Pin6, Part1.D6_PWM
  N7: Keypad4x4.Pin7, Part1.D5_PWM
  N8: Keypad4x4.Pin8, Part1.D4
  N9: Part1.A4/SDA, LCM1602_IIC1.SDA
  5V: Part1.5V, LCM1602_IIC1.VCC
  GND: Part1.GND, LCM1602_IIC1.GND, R1.Pin_0, J1.pin2, M1.pin2, M1.pin5, M1.pin7
  N10: Part1.D12/MISO, J1.pin1
  N11: Part1.A5/SCL, LCM1602_IIC1.SCL
  N12: Part1.D2, LED2.cathode, M1.pin1
  N13: Part1.D3_PWM, LED1.cathode
  VSS: LCM1602_IIC1.VSS, U1.VSS
  VDD: LCM1602_IIC1.VDD, U1.VDD
  N14: LCM1602_IIC1.V0, U1.VO
  N15: LCM1602_IIC1.RS, U1.RS
  N16: LCM1602_IIC1.RW, U1.R_W
  N17: LCM1602_IIC1.E, U1.E
  N18: LCM1602_IIC1.D0, U1.DB0
  N19: LCM1602_IIC1.D1, U1.DB1
  N20: LCM1602_IIC1.D2, U1.DB2
  N21: LCM1602_IIC1.D3, U1.DB3
  N22: LCM1602_IIC1.D4, U1.DB4
  N23: LCM1602_IIC1.D5, U1.DB5
  N24: LCM1602_IIC1.D6, U1.DB6
  N25: LCM1602_IIC1.D7, U1.DB7
  N26: LCM1602_IIC1.A, U1.A
  N27: LCM1602_IIC1.K, U1.K
  N28: M1.pin9, L1.pin2
  N29: M1.pin10, L1.pin1

custom parts:
  Keypad Membran 4x4: Membrane Keypad 4x4 Matrix
  LCM1602 IIC: I2C-Module to use a 1602 or 2004 LCD on with the wire.h libory Serial LCD Modul
  xy-mos d4184: xy-mos d4184 Two parallel N-Channel logic compatible MOSFETS with low Rds(on) for high current low-side switching applications.
